// Logisim project Lab - 2 (1).circ as structural Verilog
module XOR_using_NOR (
  input  in_1,
  input  in_2,
  output out_3
);

  wire nor_1_out, nor_2_out, nor_3_out, nor_4_out;

  nor nor_1 (nor_1_out, in_1, in_1);
  nor nor_2 (nor_2_out, in_2, in_2);
  nor nor_3 (nor_3_out, in_1, in_2);
  nor nor_4 (nor_4_out, nor_1_out, nor_2_out);
  nor nor_5 (out_3, nor_4_out, nor_3_out);
endmodule
