// Logisim project Second Canonical Function.circ as structural Verilog: 2 circuits, main circuit main
module main (
  input  in_1,
  input  in_2,
  input  in_3,
  output out_4
);

  Second_Canonical_Function second_canonical_function_1 (.A(in_1), .B(in_2), .C(in_3), .F(out_4));
endmodule

module Second_Canonical_Function (
  input  A,
  input  B,
  input  C,
  output F
);

  wire _1_out, _2_out, _3_out, _4_out, _5_out, and_1_out, and_2_out, not_1_out;

  not not_1 (not_1_out, A);
  not not_2 (not_1_out, B);
  not not_3 (not_1_out, C);
  or _4 (_4_out, not_1_out, B, not_1_out);
  or _1 (_1_out, A, B, C);
  or _2 (_2_out, A, not_1_out, not_1_out);
  or _3 (_3_out, not_1_out, B, C);
  or _5 (_5_out, not_1_out, not_1_out, not_1_out);
  and and_1 (and_1_out, _1_out, _2_out, _3_out);
  and and_2 (and_2_out, _4_out, _5_out);
  and and_3 (F, and_1_out, and_2_out);
endmodule
