// Logisim project First Canonical Function.circ as structural Verilog: 2 circuits, main circuit main
module main (
  input  in_1,
  input  in_2,
  input  in_3,
  output out_4
);

  First_Canonical_Function first_canonical_function_1 (.A(in_1), .B(in_2), .C(in_3), .F(out_4));
endmodule

module First_Canonical_Function (
  input  A,
  input  B,
  input  C,
  output F
);

  wire and_1_out, and_2_out, and_3_out, not_1_out, not_2_out, not_3_out;

  not not_1 (not_1_out, A);
  not not_2 (not_2_out, B);
  not not_3 (not_3_out, C);
  and and_1 (and_1_out, A, B, not_3_out);
  and and_2 (and_2_out, not_1_out, not_2_out, C);
  and and_3 (and_3_out, not_1_out, B, not_3_out);
  or or_1 (F, and_2_out, and_3_out, and_1_out);
endmodule
