// Logisim project XNOR using NOR.circ as structural Verilog
module XNOR_using_NOR (
  input  in_1,
  input  in_2,
  output out_3
);

  wire nor_1_out, nor_2_out, nor_3_out;

  nor nor_1 (nor_1_out, in_1, in_2);
  nor nor_2 (nor_2_out, in_1, nor_1_out);
  nor nor_3 (nor_3_out, nor_1_out, in_2);
  nor nor_4 (out_3, nor_2_out, nor_3_out);
endmodule
